# Fritzing sketch Projeto_final (saved by Fritzing 0.9.3b)
breadboards: 1

parts:
  Componente1 = Arduino Uno (Rev3)
  DHT1 = DHT11 Humitidy and Temperature Sensor
  J1 = Piezo Speaker
  U1 = GAS_SENSOR [package=mq-3]

nets:
  N1: Componente1.A1, DHT1.DATA
  5V: Componente1.5V, DHT1.VDD, J1.pin2, U1.A1
  GND: Componente1.GND, DHT1.GND, J1.pin1, U1.B1

custom parts:
  DHT11 Humitidy and Temperature Sensor: DHT11 Humidity and Temperature Sensor
